# Fritzing sketch SPI_BUS (saved by Fritzing 0.9.3b)

parts:
  Part1 = Arduino Nano (Rev3.0)
  Part2 = Arduino Uno (Rev3)

nets:
  GND: Part1.GND, Part2.GND
  N1: Part1.D10, Part2.D10_PWM/SS
  N2: Part1.D11/MOSI, Part2.D11_PWM/MOSI
  N3: Part1.D12/MISO, Part2.D12/MISO
  N4: Part1.D13/SCK, Part2.D13/SCK

// code stored in the sketch: SPI-Master.ino
#include <SPI.h>

void setup() {
	pinMode(SS, OUTPUT);
	digitalWrite(SS, HIGH);
	SPI.begin();
	SPI.setClockDivider(SPI_CLOCK_DIV8);
}

void loop() {
	digitalWrite(SS, LOW);
	SPI.transfer(5318);
	digitalWrite(SS, HIGH);
	delay(1000);
}

// code stored in the sketch: SPI-Slave.ino
#include <SPI.h>

volatile int num = 0;

void setup() {
 	pinMode(MISO, OUTPUT);
	SPCR |= _BV(SPE);
	SPI.attachInterrupt();

	Serial.begin(9600);
}

void loop() {
	Serial.println(num);
}

ISR(SPI_STC_vect) {
	num = int(SPDR);
	Serial.println("num Updated!");
}

// code stored in the sketch: SPI_Master.ino
// Arduino UNO: Reading the signals and sending over SPI.

#include <SPI.h>

void setup() {
  pinMode(SS, OUTPUT);
  digitalWrite(SS, HIGH);
  SPI.begin();
  SPI.setClockDivider(SPI_CLOCK_DIV8);
}

void loop() {
    digitalWrite(SS, LOW);
    SPI.transfer(val);
    digitalWrite(SS, HIGH);
}
